# Fritzing sketch adc_potentiometer (saved by Fritzing 0.9.3b)
breadboards: 1

parts:
  Part3 = Arduino Uno (Rev3)
  R1 = Rotary Potentiometer (Small) [maximum_resistance=100kΩ package=THT]

nets:
  N1: Part3.A0, R1.wiper
  N2: Part3.GND, R1.leg1
  N3: Part3.5V, R1.leg2
