# Fritzing sketch blink (saved by Fritzing 0.9.3b)
breadboards: 1

parts:
  Part2 = Arduino Uno (Rev3)
  R4 = Resistor [tolerance=±5% resistance=220 package=THT]
  LED2 = LED - 5mm [color="Red (633nm)" package="5 mm [THT]"]

nets:
  N1: Part2.D13/SCK, R4.Pin_1
  N2: Part2.GND, LED2.cathode
  N3: R4.Pin_0, LED2.anode
