# Fritzing sketch button (saved by Fritzing 0.9.3b)
breadboards: 1

parts:
  S1 = Pushbutton [package="[THT]"]
  Part1 = Arduino Uno (Rev3)
  R1 = Resistor [tolerance=±5% resistance=220 package=THT]
  R2 = Resistor [tolerance=±5% resistance=220 package=THT]
  LED1 = LED - 5mm [color="Red (633nm)" package="5 mm [THT]"]

nets:
  N1: S1.Pin_1, S1.Pin_2, Part1.D8, R1.Pin_1
  N2: S1.Pin_3, S1.Pin_4, Part1.GND, LED1.cathode
  N3: Part1.D13/SCK, R2.Pin_1
  N4: Part1.5V, R1.Pin_0
  N5: R2.Pin_0, LED1.anode
