# Fritzing sketch hc06_bluetooth (saved by Fritzing 0.9.3b)
breadboards: 1

parts:
  Part4 = Arduino Uno (Rev3)
  Part5 = Bluetooth HC-05 Macho

nets:
  GND: Part4.GND, Part5.GND
  N1: Part4.D0/RX, Part5.TXD
  N2: Part4.D1/TX, Part5.RXD
  5V: Part4.5V, Part5.VCC
