# Fritzing sketch lb1630_dc_motor (saved by Fritzing 0.9.3b)
breadboards: 1

parts:
  S1 = Pushbutton [package="[THT]"]
  Part1 = Arduino Uno (Rev3)
  R1 = Resistor [tolerance=±5% resistance=220 package=THT]
  R2 = Resistor [tolerance=±5% resistance=220 package=THT]
  LED1 = LED - 5mm [color="Red (633nm)" package="5 mm [THT]"]
  IC1 = Hex Inverter Schmitt Trigger SN74HC14 [package="DIP (Dual Inline)"]
  C1 = Capacitor [package=cap-pth-small2]
  R3 = Resistor [tolerance=±5% resistance=220 package=THT]
  IC2 = PICAXE-08 [package=THT]
  C2 = Electrolytic Capacitor [capacitance=1000μF package="1010 [SMD, electrolytic]"]
  M1 = DC Motor

nets:
  N1: S1.Pin_1, S1.Pin_2, R1.Pin_0, R2.Pin_0
  GND: S1.Pin_3, S1.Pin_4, Part1.GND, LED1.cathode, IC1.GND, C1.1, IC2.Serial_In, C2.-
  N2: Part1.D11_PWM/MOSI, IC2.In_3
  N3: Part1.D12/MISO, R3.Pin_1
  N4: Part1.D13/SCK, IC1.1Y
  N5: Part1.D3_PWM, IC2.+V
  5V: Part1.5V, R1.Pin_1, IC1.VCC, IC2.Serial_Out_/_Out_0, C2.+
  N6: R2.Pin_1, IC1.1A, C1.2
  N7: LED1.anode, R3.Pin_0
  N8: IC2.In/Out_2, M1.pin_2
  N9: IC2.0V, M1.pin_1
