# Fritzing sketch ms5611_test (saved by Fritzing 0.9.3b)
breadboards: 1

parts:
  Part4 = Arduino Uno (Rev3)
  Part5 = IMU Digital Combo Board 6DOF

nets:
  GND: Part4.GND, Part5.GND
  N1: Part4.D0/RX, Part5.SCL
  N2: Part4.D1/TX, Part5.SDA
  5V: Part4.5V, Part5.3.3V
