# Fritzing sketch oc_circuit_based_7805 (saved by Fritzing 0.9.3b)
breadboards: 1

parts:
  Part3 = Arduino Uno (Rev3)
  IC1 = Voltage Regulator [package=to-220-alt]
  Q1 = NPN-Transistor [package="SOT-23 [SMD]"]
  R5 = Resistor [tolerance=±5% resistance=220 package=THT]
  R6 = Resistor [tolerance=±5% resistance=220 package=THT]
  LED3 = LED - 5mm [color="Red (633nm)" package="5 mm [THT]"]
  VCC1 = Battery block 9V
  C1 = Electrolytic Capacitor [capacitance=1µF package="100 mil [THT, electrolytic]"]
  C2 = Electrolytic Capacitor [capacitance=1µF package="100 mil [THT, electrolytic]"]

nets:
  N1: Part3.D8, R5.Pin_0
  N2: Part3.GND, IC1.IN, Q1.2, VCC1.-, C1.+, C2.-
  N3: IC1.GND, VCC1.+, C1.-
  N4: IC1.OUT, R6.Pin_1, C2.+
  N5: Q1.0, R5.Pin_1
  N6: Q1.1, LED3.cathode
  N7: R6.Pin_0, LED3.anode
