# Fritzing sketch pwm_led (saved by Fritzing 0.9.3b)
breadboards: 1

parts:
  Part3 = Arduino Uno (Rev3)
  R5 = Resistor [tolerance=±5% resistance=220 package=THT]
  LED3 = LED - 5mm [color="Red (633nm)" package="5 mm [THT]"]

nets:
  N1: Part3.D9_PWM, R5.Pin_1
  N2: Part3.GND, LED3.cathode
  N3: R5.Pin_0, LED3.anode
