# Fritzing sketch schmitt_trigger_button (saved by Fritzing 0.9.3b)
breadboards: 1

parts:
  S1 = Pushbutton [package="[THT]"]
  Part1 = Arduino Uno (Rev3)
  R1 = Resistor [tolerance=±5% resistance=220 package=THT]
  R2 = Resistor [tolerance=±5% resistance=220 package=THT]
  LED1 = LED - 5mm [color="Red (633nm)" package="5 mm [THT]"]
  IC1 = Hex Inverter Schmitt Trigger SN74HC14 [package="DIP (Dual Inline)"]
  C1 = Capacitor [package=cap-pth-small2]
  R3 = Resistor [tolerance=±5% resistance=220 package=THT]

nets:
  N1: S1.Pin_1, S1.Pin_2, R1.Pin_0, R2.Pin_0
  GND: S1.Pin_3, S1.Pin_4, Part1.GND, LED1.cathode, IC1.GND, C1.1
  N2: Part1.D12/MISO, R3.Pin_1
  N3: Part1.D13/SCK, IC1.1Y
  5V: Part1.5V, R1.Pin_1, IC1.VCC
  N4: R2.Pin_1, IC1.1A, C1.2
  N5: LED1.anode, R3.Pin_0
