# Fritzing sketch seven_segment_4digit (saved by Fritzing 0.9.3b)
breadboards: 1

parts:
  Part2 = Arduino Uno (Rev3)
  R13 = Resistor [tolerance=±5% resistance=220 package=THT]
  R14 = Resistor [tolerance=±5% resistance=220 package=THT]
  R15 = Resistor [tolerance=±5% resistance=220 package=THT]
  R16 = Resistor [tolerance=±5% resistance=220 package=THT]
  R17 = Resistor [tolerance=±5% resistance=220 package=THT]
  R18 = Resistor [tolerance=±5% resistance=220 package=THT]
  R19 = Resistor [tolerance=±5% resistance=220 package=THT]
  R20 = Resistor [tolerance=±5% resistance=220 package=THT]
  LED2 = 7-SEGMENT-4DIGIT-YOUNGSUN [package=7-segment-4digit-youngsun-longpads]
  Q5 = NPN-Transistor [package="TO92 [THT]"]
  Q6 = NPN-Transistor [package="TO92 [THT]"]
  Q7 = NPN-Transistor [package="TO92 [THT]"]
  Q8 = NPN-Transistor [package="TO92 [THT]"]
  R21 = Resistor [tolerance=±5% resistance=220 package=THT]
  R22 = Resistor [tolerance=±5% resistance=220 package=THT]
  R23 = Resistor [tolerance=±5% resistance=220 package=THT]
  R24 = Resistor [tolerance=±5% resistance=220 package=THT]

nets:
  N1: Part2.D8, R21.Pin_1
  N2: Part2.D9_PWM, R22.Pin_1
  N3: Part2.D10_PWM/SS, R23.Pin_1
  N4: Part2.D11_PWM/MOSI, R24.Pin_0
  N5: Part2.GND, Q5.E, Q6.E, Q7.E, Q8.E
  N6: Part2.D1/TX, R15.Pin_1
  N7: Part2.D2, R17.Pin_1
  N8: Part2.D3_PWM, R14.Pin_0
  N9: Part2.D4, R16.Pin_0
  N10: Part2.D5_PWM, R13.Pin_0
  N11: Part2.D6_PWM, R18.Pin_1
  N12: Part2.D7, R19.Pin_0
  N13: R13.Pin_1, LED2.C
  N14: R14.Pin_1, LED2.D
  N15: R15.Pin_0, LED2.APOS-A
  N16: R16.Pin_1, LED2.DIG2
  N17: R17.Pin_0, LED2.E
  N18: R18.Pin_0, LED2.DIG3
  N19: R19.Pin_1, LED2.COL-A
  N20: R20.Pin_1, LED2.A
  N21: LED2.DP, Q8.C
  N22: LED2.F, Q7.C
  N23: LED2.COL-C, Q6.C
  N24: LED2.G, Q5.C
  N25: Q5.B, R21.Pin_0
  N26: Q6.B, R22.Pin_0
  N27: Q7.B, R23.Pin_0
  N28: Q8.B, R24.Pin_1
