# Fritzing sketch spi_25lc010 (saved by Fritzing 0.9.3b)
breadboards: 1

parts:
  Part4 = Arduino Uno (Rev3)
  IC1 = 25LC010 [package=THT]

nets:
  N1: Part4.D10_PWM/SS, IC1.CS_-_Chip_Select
  N2: Part4.D11_PWM/MOSI, IC1.SI_-_Data_In
  N3: Part4.D12/MISO, IC1.SO_-_Data_Out
  N4: Part4.D13/SCK, IC1.SCK_-_SPI_Clock
  N5: Part4.5V, IC1.WP_-_Write_Protect, IC1.0V, IC1.HOLD, IC1.+V
