# Fritzing sketch text_lcd_8bit_mode (saved by Fritzing 0.9.3b)
breadboards: 1

parts:
  Part4 = Arduino Uno (Rev3)
  LCD1 = LCD screen
  R1 = Rotary Potentiometer (Small) [maximum_resistance=100kΩ package=THT]
  R2 = Resistor [tolerance=±5% resistance=220 package=THT]

nets:
  N1: Part4.D8, LCD1.RS
  N2: Part4.D9_PWM, LCD1.E
  GND: Part4.GND, LCD1.VSS, LCD1.R/W, LCD1.LED-
  N3: Part4.D0/RX, LCD1.DB0
  N4: Part4.D1/TX, LCD1.DB1
  N5: Part4.D2, LCD1.DB2
  N6: Part4.D3_PWM, LCD1.DB3
  N7: Part4.D4, LCD1.DB4
  N8: Part4.D5_PWM, LCD1.DB5
  N9: Part4.D6_PWM, LCD1.DB6
  N10: Part4.D7, LCD1.DB7
  5V: Part4.5V, LCD1.VDD, R1.leg1, R1.leg2, R2.Pin_1
  N11: LCD1.V0, R1.wiper
  N12: LCD1.LED+, R2.Pin_0
